// Logisim project playground.circ as structural Verilog: 10 circuits, main circuit main
module main (
  input  [7:0] in_1,
  input  [7:0] in_2,
  input  in_3,
  output [7:0] out_4,
  output [7:0] out_5,
  output [7:0] out_6,
  output [7:0] out_7,
  output out_8
);

  byte_add_sub byte_add_sub_1 (.overflow(out_8), .D(out_6), .B(in_2), .A(in_1));  // open: Sub

  assign out_4 = in_1;
  assign out_5 = in_2;
  assign out_7 = out_6;
endmodule

module my_xor (
  input  A,
  input  B,
  output D
);

  wire AND_out, NOT_out, OR_out;

  and AND (AND_out, A, B);
  not NOT (NOT_out, AND_out);
  or OR (OR_out, A, B);
  and AND_2 (D, NOT_out, OR_out);
endmodule

module bit_adder (
  input  A,
  input  B,
  input  carry,
  output D,
  output carry_2
);

  wire AND_2_out, AND_3_out, AND_out, XOR_out;

  xor XOR (XOR_out, A, B);
  and AND (AND_out, A, B);
  and AND_2 (AND_2_out, A, carry);
  xor XOR_2 (D, XOR_out, carry);
  and AND_3 (AND_3_out, B, carry);
  or OR (carry_2, AND_out, AND_2_out, AND_3_out);
endmodule

module half_byte_adder (
  input  A_3,
  input  A_2,
  input  A_1,
  input  A_0,
  input  B_3,
  input  B_2,
  input  B_1,
  input  B_0,
  input  in_9,
  output out_10,
  output out_11,
  output out_12,
  output out_13
);

  wire bit_adder_1_carry_2, bit_adder_2_carry_2, bit_adder_3_carry_2;

  bit_adder bit_adder_1 (.D(out_10), .carry_2(bit_adder_1_carry_2), .A(A_0), .B(B_0), .carry(in_9));
  bit_adder bit_adder_2 (.D(out_11), .carry_2(bit_adder_2_carry_2), .A(A_1), .B(B_1), .carry(bit_adder_1_carry_2));
  bit_adder bit_adder_3 (.D(out_12), .carry_2(bit_adder_3_carry_2), .A(A_2), .B(B_2), .carry(bit_adder_2_carry_2));
  bit_adder bit_adder_4 (.D(out_13), .A(A_3), .B(B_3), .carry(bit_adder_3_carry_2));  // open: carry_2
endmodule

module byte_adder (
  input  carry,
  input  [7:0] A,
  input  [7:0] B,
  output [7:0] D,
  output overflow
);

  wire bit_adder_1_carry_2, bit_adder_2_carry_2, bit_adder_3_carry_2, bit_adder_4_carry_2,
       bit_adder_5_carry_2, bit_adder_6_carry_2, bit_adder_7_carry_2;

  bit_adder bit_adder_1 (.D(D[0]), .carry_2(bit_adder_1_carry_2), .A(A[0]), .B(B[0]), .carry(carry));
  bit_adder bit_adder_2 (.D(D[1]), .carry_2(bit_adder_2_carry_2), .A(A[1]), .B(B[1]), .carry(bit_adder_1_carry_2));
  bit_adder bit_adder_3 (.D(D[2]), .carry_2(bit_adder_3_carry_2), .A(A[2]), .B(B[2]), .carry(bit_adder_2_carry_2));
  bit_adder bit_adder_4 (.D(D[3]), .carry_2(bit_adder_4_carry_2), .A(A[3]), .B(B[3]), .carry(bit_adder_3_carry_2));
  bit_adder bit_adder_5 (.D(D[4]), .carry_2(bit_adder_5_carry_2), .A(A[4]), .B(B[4]), .carry(bit_adder_4_carry_2));
  bit_adder bit_adder_6 (.D(D[5]), .carry_2(bit_adder_6_carry_2), .A(A[5]), .B(B[5]), .carry(bit_adder_5_carry_2));
  bit_adder bit_adder_7 (.D(D[6]), .carry_2(bit_adder_7_carry_2), .A(A[6]), .B(B[6]), .carry(bit_adder_6_carry_2));
  bit_adder bit_adder_8 (.D(D[7]), .carry_2(overflow), .A(A[7]), .B(B[7]), .carry(bit_adder_7_carry_2));
endmodule

module negate (
  input  Neg,
  input  [7:0] In,
  output [7:0] out
);

  xor xor_1 (out[0], In[0], Neg);
  xor xor_2 (out[1], In[1], Neg);
  xor xor_3 (out[2], In[2], Neg);
  xor xor_4 (out[3], In[3], Neg);
  xor xor_5 (out[4], In[4], Neg);
  xor xor_6 (out[5], In[5], Neg);
  xor xor_7 (out[6], In[6], Neg);
  xor xor_8 (out[7], In[7], Neg);
endmodule

module add_sub (
  input  Sub,
  input  [7:0] A,
  input  [7:0] B,
  output [7:0] Out,
  output carry,
  output Negative
);

  wire [7:0] negate_1_out;

  negate negate_1 (.out(negate_1_out), .In(B), .Neg(Sub));
  byte_adder byte_adder_1 (.overflow(carry), .D({Negative, Out[6:0]}), .B(negate_1_out), .A(A), .carry(Sub));

  assign Out[7] = Negative;
endmodule

module new_xor (
  input  A,
  input  B,
  output out_3
);

  wire AND_out, not_1_out, OR_2_out, OR_out;

  and AND (AND_out, A, B);
  or OR (OR_out, A, B);
  not not_1 (not_1_out, OR_out);
  or OR_2 (OR_2_out, AND_out, not_1_out);
  not not_2 (out_3, OR_2_out);
endmodule

module simple_add (
  input  A,
  input  B,
  input  C,
  output D
);

  wire XOR_out;

  xor XOR (XOR_out, A, B);
  xor XOR_2 (D, XOR_out, C);
endmodule

module byte_add_sub (
  input  Sub,
  input  [7:0] A,
  input  [7:0] B,
  output [7:0] D,
  output overflow
);

  wire bit_adder_1_carry_2, bit_adder_2_carry_2, bit_adder_3_carry_2, bit_adder_4_carry_2,
       bit_adder_5_carry_2, bit_adder_6_carry_2, bit_adder_7_carry_2;
  wire [7:0] negate_1_out;

  negate negate_1 (.out(negate_1_out), .In(B), .Neg(Sub));
  bit_adder bit_adder_1 (.D(D[0]), .carry_2(bit_adder_1_carry_2), .A(A[0]), .B(negate_1_out[0]), .carry(Sub));
  bit_adder bit_adder_2 (
    .D(D[1]), .carry_2(bit_adder_2_carry_2), .A(A[1]), .B(negate_1_out[1]), .carry(bit_adder_1_carry_2));
  bit_adder bit_adder_3 (
    .D(D[2]), .carry_2(bit_adder_3_carry_2), .A(A[2]), .B(negate_1_out[2]), .carry(bit_adder_2_carry_2));
  bit_adder bit_adder_4 (
    .D(D[3]), .carry_2(bit_adder_4_carry_2), .A(A[3]), .B(negate_1_out[3]), .carry(bit_adder_3_carry_2));
  bit_adder bit_adder_5 (
    .D(D[4]), .carry_2(bit_adder_5_carry_2), .A(A[4]), .B(negate_1_out[4]), .carry(bit_adder_4_carry_2));
  bit_adder bit_adder_6 (
    .D(D[5]), .carry_2(bit_adder_6_carry_2), .A(A[5]), .B(negate_1_out[5]), .carry(bit_adder_5_carry_2));
  bit_adder bit_adder_7 (
    .D(D[6]), .carry_2(bit_adder_7_carry_2), .A(A[6]), .B(negate_1_out[6]), .carry(bit_adder_6_carry_2));
  bit_adder bit_adder_8 (.D(D[7]), .carry_2(overflow), .A(A[7]), .B(negate_1_out[7]), .carry(bit_adder_7_carry_2));
endmodule
